// Logisim project 332L Project.circ as structural Verilog
module main (
  output [27:0] Result,
  output out_2
);

  wire and_1_out, and_2_out, clock_1_out, control_unit_1_alusrc, control_unit_1_binv, control_unit_1_bne,
       control_unit_1_branch, control_unit_1_jump, control_unit_1_memread, control_unit_1_memwrt,
       control_unit_1_regdst, control_unit_1_regwrt, control_unit_1_signzero, n28_bit_alu_1_zero_flag,
       not_1_out, or_1_out;
  wire [1:0] control_unit_1_memtoreg;
  wire [2:0] control_unit_1_aluop;
  wire [4:0] instruction_memory_1_instruction_2, multiplexer_1_out;
  wire [6:0] adder_1_out, adder_2_out, bit_extender_2_out, bit_extender_3_out, multiplexer_3_out,
       multiplexer_5_out, register_1_q;
  wire [14:0] instruction_memory_1_instruction;
  wire [27:0] bit_extender_1_out, data_memory_1_readdata, multiplexer_2_out, n28_bit_alu_1_result,
       register_file_1_read_data_1, register_file_1_read_data_2, shifter_1_out, shifter_2_out;

  Clock clock_1 (.out(clock_1_out));
  Register #(.width(7)) register_1 (.D(multiplexer_5_out), .Q(register_1_q), .clk(clock_1_out));  // open: en, clr
  Adder #(.width(7)) adder_1 (.a(register_1_q), .b({7{1'b0}}), .out(adder_1_out), .cin(1'b0));  // open: cout
  Instruction_Memory instruction_memory_1 (
    .Address(register_1_q),
    .Instruction({instruction_memory_1_instruction_2, instruction_memory_1_instruction}));
  Control_Unit control_unit_1 (
    .Opcode(instruction_memory_1_instruction_2), .RegWRT(control_unit_1_regwrt),
    .RegDST(control_unit_1_regdst), .AluSRC(control_unit_1_alusrc), .MemREAD(control_unit_1_memread),
    .MemWRT(control_unit_1_memwrt), .MemToReg(control_unit_1_memtoreg), .Branch(control_unit_1_branch),
    .BNE(control_unit_1_bne), .Jump(control_unit_1_jump), .SignZero(control_unit_1_signzero),
    .AluOP(control_unit_1_aluop), .Binv(control_unit_1_binv));
  Multiplexer #(.width(5), .enable("false")) multiplexer_1 (
    .in0(instruction_memory_1_instruction[4:0]), .in1(instruction_memory_1_instruction[9:5]),
    .out(multiplexer_1_out), .sel(control_unit_1_regdst));
  Register_File register_file_1 (
    .Write_Reg_RD(multiplexer_1_out), .Write_Data(Result), .Read_Data_1(register_file_1_read_data_1),
    .Read_Reg_1_RS(instruction_memory_1_instruction[14:10]), .Read_Data_2(register_file_1_read_data_2),
    .Read_Reg_2_RT(instruction_memory_1_instruction[9:5]), .Write_Control(control_unit_1_regwrt),
    .CLK(clock_1_out));
  assign bit_extender_1_out = {{23{control_unit_1_signzero}}, instruction_memory_1_instruction[4:0]};  // Bit_Extender bit_extender_1
  Multiplexer #(.width(28), .enable("false")) multiplexer_2 (
    .in0(register_file_1_read_data_2), .in1(bit_extender_1_out), .out(multiplexer_2_out),
    .sel(control_unit_1_alusrc));
  assign bit_extender_2_out = {{2{1'b0}}, instruction_memory_1_instruction[4:0]};  // Bit_Extender bit_extender_2
  _28_bit_ALU u_28_bit_alu_1 (
    .Result(n28_bit_alu_1_result), .Zero_Flag(n28_bit_alu_1_zero_flag), .A(register_file_1_read_data_1),
    .B(multiplexer_2_out), .Select(control_unit_1_aluop), .Cin(control_unit_1_binv),
    .Binv(control_unit_1_binv), .Cout(out_2));  // open: Overflow
  Shifter #(.width(28)) shifter_1 (
    .in(register_file_1_read_data_1), .\dist (instruction_memory_1_instruction[4:0]), .out(shifter_1_out));
  Shifter #(.width(28), .shift("lr")) shifter_2 (
    .in(register_file_1_read_data_1), .\dist (instruction_memory_1_instruction[4:0]), .out(shifter_2_out));
  Adder #(.width(7)) adder_2 (.a(adder_1_out), .b(bit_extender_2_out), .out(adder_2_out));  // open: cin, cout
  not not_1 (not_1_out, n28_bit_alu_1_zero_flag);
  and and_1 (and_1_out, n28_bit_alu_1_zero_flag, control_unit_1_branch);
  and and_2 (and_2_out, not_1_out, control_unit_1_bne);
  assign bit_extender_3_out = {{2{1'b0}}, instruction_memory_1_instruction[4:0]};  // Bit_Extender bit_extender_3
  or or_1 (or_1_out, and_1_out, and_2_out);
  Data_Memory data_memory_1 (
    .ADDRESS(n28_bit_alu_1_result[8:0]), .ReadData(data_memory_1_readdata),
    .Write_Data(register_file_1_read_data_2), .STR(control_unit_1_memwrt), .Load(control_unit_1_memread),
    .in_4(clock_1_out));  // open: Clr
  Multiplexer #(.width(7), .enable("false")) multiplexer_3 (
    .in0(adder_1_out), .in1(adder_2_out), .out(multiplexer_3_out), .sel(or_1_out));
  Multiplexer #(.select(2), .width(28), .enable("false")) multiplexer_4 (
    .in0(n28_bit_alu_1_result), .in1(shifter_1_out), .in2(shifter_2_out), .in3(data_memory_1_readdata),
    .out(Result), .sel(control_unit_1_memtoreg));
  Multiplexer #(.width(7), .enable("false")) multiplexer_5 (
    .in0(multiplexer_3_out), .in1(bit_extender_3_out), .out(multiplexer_5_out), .sel(control_unit_1_jump));

  // Notes on the sheet:
  //   shift left
  //   shift right
endmodule

module Register_File (
  input  [4:0] Write_Reg_RD,
  input  [4:0] Read_Reg_1_RS,
  input  [4:0] Read_Reg_2_RT,
  input  [27:0] Write_Data,
  input  Write_Control,
  input  CLK,
  output [27:0] Read_Data_1,
  output [27:0] Read_Data_2
);

  wire and_1_out, and_2_out, and_3_out, and_4_out, and_5_out, and_6_out, and_7_out, and_8_out, and_9_out,
       and_10_out, and_11_out, and_12_out, and_13_out, and_14_out, and_15_out, and_16_out, and_17_out,
       and_18_out, and_19_out, and_20_out, and_21_out, and_22_out, and_23_out, and_24_out, and_25_out,
       and_26_out, and_27_out, and_28_out, and_29_out, and_30_out, and_31_out, and_32_out, decoder_1_out0,
       decoder_1_out1, decoder_1_out2, decoder_1_out3, decoder_1_out4, decoder_1_out5, decoder_1_out6,
       decoder_1_out7, decoder_1_out8, decoder_1_out9, decoder_1_out10, decoder_1_out11, decoder_1_out12,
       decoder_1_out13, decoder_1_out14, decoder_1_out15, decoder_1_out16, decoder_1_out17, decoder_1_out18,
       decoder_1_out19, decoder_1_out20, decoder_1_out21, decoder_1_out22, decoder_1_out23, decoder_1_out24,
       decoder_1_out25, decoder_1_out26, decoder_1_out27, decoder_1_out28, decoder_1_out29, decoder_1_out30,
       decoder_1_out31;
  wire [27:0] register_1_q, register_2_q, register_3_q, register_4_q, register_5_q, register_6_q,
       register_7_q, register_8_q, register_9_q, register_10_q, register_11_q, register_12_q, register_13_q,
       register_14_q, register_15_q, register_16_q, register_17_q, register_18_q, register_19_q,
       register_20_q, register_21_q, register_22_q, register_23_q, register_24_q, register_25_q,
       register_26_q, register_27_q, register_28_q, register_29_q, register_30_q, register_31_q,
       register_32_q;

  Decoder #(.select(5), .enable("false")) decoder_1 (
    .out0(decoder_1_out0), .out1(decoder_1_out1), .out2(decoder_1_out2), .out3(decoder_1_out3),
    .out4(decoder_1_out4), .out5(decoder_1_out5), .out6(decoder_1_out6), .out7(decoder_1_out7),
    .out8(decoder_1_out8), .out9(decoder_1_out9), .out10(decoder_1_out10), .out11(decoder_1_out11),
    .out12(decoder_1_out12), .out13(decoder_1_out13), .out14(decoder_1_out14), .out15(decoder_1_out15),
    .out16(decoder_1_out16), .out17(decoder_1_out17), .out18(decoder_1_out18), .out19(decoder_1_out19),
    .out20(decoder_1_out20), .out21(decoder_1_out21), .out22(decoder_1_out22), .out23(decoder_1_out23),
    .out24(decoder_1_out24), .out25(decoder_1_out25), .out26(decoder_1_out26), .out27(decoder_1_out27),
    .out28(decoder_1_out28), .out29(decoder_1_out29), .out30(decoder_1_out30), .out31(decoder_1_out31),
    .sel(Write_Reg_RD));
  and and_1 (and_1_out, decoder_1_out0, Write_Control);
  and and_2 (and_2_out, decoder_1_out1, Write_Control);
  and and_3 (and_3_out, decoder_1_out2, Write_Control);
  and and_4 (and_4_out, decoder_1_out3, Write_Control);
  and and_5 (and_5_out, decoder_1_out4, Write_Control);
  and and_6 (and_6_out, decoder_1_out5, Write_Control);
  and and_7 (and_7_out, decoder_1_out6, Write_Control);
  and and_8 (and_8_out, decoder_1_out7, Write_Control);
  and and_9 (and_9_out, decoder_1_out8, Write_Control);
  and and_10 (and_10_out, decoder_1_out9, Write_Control);
  and and_11 (and_11_out, decoder_1_out10, Write_Control);
  and and_12 (and_12_out, decoder_1_out11, Write_Control);
  and and_13 (and_13_out, decoder_1_out12, Write_Control);
  and and_14 (and_14_out, decoder_1_out13, Write_Control);
  and and_15 (and_15_out, decoder_1_out14, Write_Control);
  and and_16 (and_16_out, decoder_1_out15, Write_Control);
  and and_17 (and_17_out, decoder_1_out16, Write_Control);
  and and_18 (and_18_out, decoder_1_out17, Write_Control);
  and and_19 (and_19_out, decoder_1_out18, Write_Control);
  and and_20 (and_20_out, decoder_1_out19, Write_Control);
  and and_21 (and_21_out, decoder_1_out20, Write_Control);
  and and_22 (and_22_out, decoder_1_out21, Write_Control);
  and and_23 (and_23_out, decoder_1_out22, Write_Control);
  and and_24 (and_24_out, decoder_1_out23, Write_Control);
  and and_25 (and_25_out, decoder_1_out24, Write_Control);
  and and_26 (and_26_out, decoder_1_out25, Write_Control);
  and and_27 (and_27_out, decoder_1_out26, Write_Control);
  and and_28 (and_28_out, decoder_1_out27, Write_Control);
  and and_29 (and_29_out, decoder_1_out28, Write_Control);
  and and_30 (and_30_out, decoder_1_out29, Write_Control);
  and and_31 (and_31_out, decoder_1_out30, Write_Control);
  and and_32 (and_32_out, decoder_1_out31, Write_Control);
  Register #(.width(28)) register_1 (.D(Write_Data), .en(and_1_out), .Q(register_1_q), .clk(CLK), .clr(1'b1));
  Register #(.width(28)) register_2 (.D(Write_Data), .en(and_2_out), .Q(register_2_q), .clk(CLK), .clr(1'b1));
  Register #(.width(28)) register_3 (.D(Write_Data), .en(and_3_out), .Q(register_3_q), .clk(CLK), .clr(1'b1));
  Register #(.width(28)) register_4 (.D(Write_Data), .en(and_4_out), .Q(register_4_q), .clk(CLK), .clr(1'b1));
  Register #(.width(28)) register_5 (.D(Write_Data), .en(and_5_out), .Q(register_5_q), .clk(CLK), .clr(1'b1));
  Register #(.width(28)) register_6 (.D(Write_Data), .en(and_6_out), .Q(register_6_q), .clk(CLK), .clr(1'b1));
  Register #(.width(28)) register_7 (.D(Write_Data), .en(and_7_out), .Q(register_7_q), .clk(CLK), .clr(1'b1));
  Register #(.width(28)) register_8 (.D(Write_Data), .en(and_8_out), .Q(register_8_q), .clk(CLK), .clr(1'b1));
  Register #(.width(28)) register_9 (.D(Write_Data), .en(and_9_out), .Q(register_9_q), .clk(CLK), .clr(1'b1));
  Register #(.width(28)) register_10 (.D(Write_Data), .en(and_10_out), .Q(register_10_q), .clk(CLK), .clr(1'b1));
  Register #(.width(28)) register_11 (.D(Write_Data), .en(and_11_out), .Q(register_11_q), .clk(CLK), .clr(1'b1));
  Register #(.width(28)) register_12 (.D(Write_Data), .en(and_12_out), .Q(register_12_q), .clk(CLK), .clr(1'b1));
  Register #(.width(28)) register_13 (.D(Write_Data), .en(and_13_out), .Q(register_13_q), .clk(CLK), .clr(1'b1));
  Register #(.width(28)) register_14 (.D(Write_Data), .en(and_14_out), .Q(register_14_q), .clk(CLK), .clr(1'b1));
  Register #(.width(28)) register_15 (.D(Write_Data), .en(and_15_out), .Q(register_15_q), .clk(CLK), .clr(1'b1));
  Register #(.width(28)) register_16 (.D(Write_Data), .en(and_16_out), .Q(register_16_q), .clk(CLK), .clr(1'b1));
  Register #(.width(28)) register_17 (.D(Write_Data), .en(and_17_out), .Q(register_17_q), .clk(CLK), .clr(1'b1));
  Register #(.width(28)) register_18 (.D(Write_Data), .en(and_18_out), .Q(register_18_q), .clk(CLK), .clr(1'b1));
  Register #(.width(28)) register_19 (.D(Write_Data), .en(and_19_out), .Q(register_19_q), .clk(CLK), .clr(1'b1));
  Register #(.width(28)) register_20 (.D(Write_Data), .en(and_20_out), .Q(register_20_q), .clk(CLK), .clr(1'b1));
  Register #(.width(28)) register_21 (.D(Write_Data), .en(and_21_out), .Q(register_21_q), .clk(CLK), .clr(1'b1));
  Register #(.width(28)) register_22 (.D(Write_Data), .en(and_22_out), .Q(register_22_q), .clk(CLK), .clr(1'b1));
  Register #(.width(28)) register_23 (.D(Write_Data), .en(and_23_out), .Q(register_23_q), .clk(CLK), .clr(1'b1));
  Register #(.width(28)) register_24 (.D(Write_Data), .en(and_24_out), .Q(register_24_q), .clk(CLK), .clr(1'b1));
  Register #(.width(28)) register_25 (.D(Write_Data), .en(and_25_out), .Q(register_25_q), .clk(CLK), .clr(1'b1));
  Register #(.width(28)) register_26 (.D(Write_Data), .en(and_26_out), .Q(register_26_q), .clk(CLK), .clr(1'b1));
  Register #(.width(28)) register_27 (.D(Write_Data), .en(and_27_out), .Q(register_27_q), .clk(CLK), .clr(1'b1));
  Register #(.width(28)) register_28 (.D(Write_Data), .en(and_28_out), .Q(register_28_q), .clk(CLK), .clr(1'b1));
  Register #(.width(28)) register_29 (.D(Write_Data), .en(and_29_out), .Q(register_29_q), .clk(CLK), .clr(1'b1));
  Register #(.width(28)) register_30 (.D(Write_Data), .en(and_30_out), .Q(register_30_q), .clk(CLK), .clr(1'b1));
  Register #(.width(28)) register_31 (.D(Write_Data), .en(and_31_out), .Q(register_31_q), .clk(CLK), .clr(1'b1));
  Register #(.width(28)) register_32 (.D(Write_Data), .en(and_32_out), .Q(register_32_q), .clk(CLK), .clr(1'b1));
  Multiplexer #(.select(5), .width(28)) multiplexer_1 (
    .in0(register_1_q), .in1(register_2_q), .in2(register_3_q), .in3(register_4_q), .in4(register_5_q),
    .in5(register_6_q), .in6(register_7_q), .in7(register_8_q), .in8(register_9_q), .in9(register_10_q),
    .in10(register_11_q), .in11(register_12_q), .in12(register_13_q), .in13(register_14_q),
    .in14(register_15_q), .in15(register_16_q), .in16(register_17_q), .in17(register_18_q),
    .in18(register_19_q), .in19(register_20_q), .in20(register_21_q), .in21(register_22_q),
    .in22(register_23_q), .in23(register_24_q), .in24(register_25_q), .in25(register_26_q),
    .in26(register_27_q), .in27(register_28_q), .in28(register_29_q), .in29(register_30_q),
    .in30(register_31_q), .in31(register_32_q), .out(Read_Data_1), .sel(Read_Reg_1_RS));  // open: en
  Multiplexer #(.select(5), .width(28)) multiplexer_2 (
    .in0(register_1_q), .in1(register_2_q), .in2(register_3_q), .in3(register_4_q), .in4(register_5_q),
    .in5(register_6_q), .in6(register_7_q), .in7(register_8_q), .in8(register_9_q), .in9(register_10_q),
    .in10(register_11_q), .in11(register_12_q), .in12(register_13_q), .in13(register_14_q),
    .in14(register_15_q), .in15(register_16_q), .in16(register_17_q), .in17(register_18_q),
    .in18(register_19_q), .in19(register_20_q), .in20(register_21_q), .in21(register_22_q),
    .in22(register_23_q), .in23(register_24_q), .in24(register_25_q), .in25(register_26_q),
    .in26(register_27_q), .in27(register_28_q), .in28(register_29_q), .in29(register_30_q),
    .in30(register_31_q), .in31(register_32_q), .out(Read_Data_2), .sel(Read_Reg_2_RT));  // open: en
endmodule

module _1_bit_ALU (
  input  A,
  input  B,
  input  Cin,
  input  [2:0] Select,
  input  Binv,
  output Result,
  output Cout
);

  wire adder_1_out, and_1_out, and_2_out, nor_1_out, or_1_out, xor_1_out, xor_2_out;

  and and_1 (and_1_out, A, B);
  or or_1 (or_1_out, A, B);
  xor xor_1 (xor_1_out, B, and_2_out);
  xor xor_2 (xor_2_out, B, A);
  nor nor_1 (nor_1_out, B, A);
  Adder #(.width(1)) adder_1 (.a(A), .b(xor_1_out), .out(adder_1_out), .cin(Cin), .cout(Cout));
  and and_2 (and_2_out, Select[0], Binv);
  Multiplexer #(.select(3)) multiplexer_1 (
    .in0(and_1_out), .in1(or_1_out), .in2(adder_1_out), .in3(adder_1_out), .in4(xor_2_out), .in5(nor_1_out),
    .in6(1'b0), .in7(1'b0), .out(Result), .sel(Select));  // open: en
endmodule

module _28_bit_ALU (
  input  [27:0] A,
  input  [27:0] B,
  input  [2:0] Select,
  input  Cin,
  input  Binv,
  output [27:0] Result,
  output Zero_Flag,
  output Overflow,
  output Cout
);

  wire n1_bit_alu_1_cout, n1_bit_alu_2_cout, n1_bit_alu_3_cout, n1_bit_alu_4_cout, n1_bit_alu_5_cout,
       n1_bit_alu_6_cout, n1_bit_alu_7_cout, n1_bit_alu_8_cout, n1_bit_alu_9_cout, n1_bit_alu_10_cout,
       n1_bit_alu_11_cout, n1_bit_alu_12_cout, n1_bit_alu_13_cout, n1_bit_alu_14_cout, n1_bit_alu_15_cout,
       n1_bit_alu_16_cout, n1_bit_alu_17_cout, n1_bit_alu_18_cout, n1_bit_alu_19_cout, n1_bit_alu_20_cout,
       n1_bit_alu_21_cout, n1_bit_alu_22_cout, n1_bit_alu_23_cout, n1_bit_alu_24_cout, n1_bit_alu_25_cout,
       n1_bit_alu_26_cout, n1_bit_alu_27_cout;

  _1_bit_ALU u_1_bit_alu_1 (
    .Result(Result[0]), .Cout(n1_bit_alu_1_cout), .Select(Select), .Binv(Binv), .A(A[0]), .B(B[0]), .Cin(Cin));
  _1_bit_ALU u_1_bit_alu_2 (
    .Result(Result[1]), .Cout(n1_bit_alu_2_cout), .Select(Select), .Binv(Binv), .A(A[1]), .B(B[1]),
    .Cin(n1_bit_alu_1_cout));
  _1_bit_ALU u_1_bit_alu_3 (
    .Result(Result[2]), .Cout(n1_bit_alu_3_cout), .Select(Select), .Binv(Binv), .A(A[2]), .B(B[2]),
    .Cin(n1_bit_alu_2_cout));
  _1_bit_ALU u_1_bit_alu_4 (
    .Result(Result[3]), .Cout(n1_bit_alu_4_cout), .Select(Select), .Binv(Binv), .A(A[3]), .B(B[3]),
    .Cin(n1_bit_alu_3_cout));
  _1_bit_ALU u_1_bit_alu_5 (
    .Result(Result[4]), .Cout(n1_bit_alu_5_cout), .Select(Select), .Binv(Binv), .A(A[4]), .B(B[4]),
    .Cin(n1_bit_alu_4_cout));
  _1_bit_ALU u_1_bit_alu_6 (
    .Result(Result[5]), .Cout(n1_bit_alu_6_cout), .Select(Select), .Binv(Binv), .A(A[5]), .B(B[5]),
    .Cin(n1_bit_alu_5_cout));
  _1_bit_ALU u_1_bit_alu_7 (
    .Result(Result[6]), .Cout(n1_bit_alu_7_cout), .Select(Select), .Binv(Binv), .A(A[6]), .B(B[6]),
    .Cin(n1_bit_alu_6_cout));
  _1_bit_ALU u_1_bit_alu_8 (
    .Result(Result[7]), .Cout(n1_bit_alu_8_cout), .Select(Select), .Binv(Binv), .A(A[7]), .B(B[7]),
    .Cin(n1_bit_alu_7_cout));
  _1_bit_ALU u_1_bit_alu_9 (
    .Result(Result[8]), .Cout(n1_bit_alu_9_cout), .Select(Select), .Binv(Binv), .A(A[8]), .B(B[8]),
    .Cin(n1_bit_alu_8_cout));
  _1_bit_ALU u_1_bit_alu_10 (
    .Result(Result[9]), .Cout(n1_bit_alu_10_cout), .Select(Select), .Binv(Binv), .A(A[9]), .B(B[9]),
    .Cin(n1_bit_alu_9_cout));
  _1_bit_ALU u_1_bit_alu_11 (
    .Result(Result[10]), .Cout(n1_bit_alu_11_cout), .Select(Select), .Binv(Binv), .A(A[10]), .B(B[10]),
    .Cin(n1_bit_alu_10_cout));
  _1_bit_ALU u_1_bit_alu_12 (
    .Result(Result[11]), .Cout(n1_bit_alu_12_cout), .Select(Select), .Binv(Binv), .A(A[11]), .B(B[11]),
    .Cin(n1_bit_alu_11_cout));
  _1_bit_ALU u_1_bit_alu_13 (
    .Result(Result[12]), .Cout(n1_bit_alu_13_cout), .Select(Select), .Binv(Binv), .A(A[12]), .B(B[12]),
    .Cin(n1_bit_alu_12_cout));
  _1_bit_ALU u_1_bit_alu_14 (
    .Result(Result[13]), .Cout(n1_bit_alu_14_cout), .Select(Select), .Binv(Binv), .A(A[13]), .B(B[13]),
    .Cin(n1_bit_alu_13_cout));
  _1_bit_ALU u_1_bit_alu_15 (
    .Result(Result[14]), .Cout(n1_bit_alu_15_cout), .Select(Select), .Binv(Binv), .A(A[14]), .B(B[14]),
    .Cin(n1_bit_alu_14_cout));
  _1_bit_ALU u_1_bit_alu_16 (
    .Result(Result[15]), .Cout(n1_bit_alu_16_cout), .Select(Select), .Binv(Binv), .A(A[15]), .B(B[15]),
    .Cin(n1_bit_alu_15_cout));
  _1_bit_ALU u_1_bit_alu_17 (
    .Result(Result[16]), .Cout(n1_bit_alu_17_cout), .Select(Select), .Binv(Binv), .A(A[16]), .B(B[16]),
    .Cin(n1_bit_alu_16_cout));
  _1_bit_ALU u_1_bit_alu_18 (
    .Result(Result[17]), .Cout(n1_bit_alu_18_cout), .Select(Select), .Binv(Binv), .A(A[17]), .B(B[17]),
    .Cin(n1_bit_alu_17_cout));
  _1_bit_ALU u_1_bit_alu_19 (
    .Result(Result[18]), .Cout(n1_bit_alu_19_cout), .Select(Select), .Binv(Binv), .A(A[18]), .B(B[18]),
    .Cin(n1_bit_alu_18_cout));
  _1_bit_ALU u_1_bit_alu_20 (
    .Result(Result[19]), .Cout(n1_bit_alu_20_cout), .Select(Select), .Binv(Binv), .A(A[19]), .B(B[19]),
    .Cin(n1_bit_alu_19_cout));
  _1_bit_ALU u_1_bit_alu_21 (
    .Result(Result[20]), .Cout(n1_bit_alu_21_cout), .Select(Select), .Binv(Binv), .A(A[20]), .B(B[20]),
    .Cin(n1_bit_alu_20_cout));
  _1_bit_ALU u_1_bit_alu_22 (
    .Result(Result[21]), .Cout(n1_bit_alu_22_cout), .Select(Select), .Binv(Binv), .A(A[21]), .B(B[21]),
    .Cin(n1_bit_alu_21_cout));
  _1_bit_ALU u_1_bit_alu_23 (
    .Result(Result[22]), .Cout(n1_bit_alu_23_cout), .Select(Select), .Binv(Binv), .A(A[22]), .B(B[22]),
    .Cin(n1_bit_alu_22_cout));
  _1_bit_ALU u_1_bit_alu_24 (
    .Result(Result[23]), .Cout(n1_bit_alu_24_cout), .Select(Select), .Binv(Binv), .A(A[23]), .B(B[23]),
    .Cin(n1_bit_alu_23_cout));
  _1_bit_ALU u_1_bit_alu_25 (
    .Result(Result[24]), .Cout(n1_bit_alu_25_cout), .Select(Select), .Binv(Binv), .A(A[24]), .B(B[24]),
    .Cin(n1_bit_alu_24_cout));
  _1_bit_ALU u_1_bit_alu_26 (
    .Result(Result[25]), .Cout(n1_bit_alu_26_cout), .Select(Select), .Binv(Binv), .A(A[25]), .B(B[25]),
    .Cin(n1_bit_alu_25_cout));
  _1_bit_ALU u_1_bit_alu_27 (
    .Result(Result[26]), .Cout(n1_bit_alu_27_cout), .Select(Select), .Binv(Binv), .A(A[26]), .B(B[26]),
    .Cin(n1_bit_alu_26_cout));
  _1_bit_ALU u_1_bit_alu_28 (
    .Result(Result[27]), .Cout(Cout), .Select(Select), .Binv(Binv), .A(A[27]), .B(B[27]),
    .Cin(n1_bit_alu_27_cout));
  xor xor_1 (Overflow, n1_bit_alu_27_cout, Cout);
  nor nor_1 (Zero_Flag, Result[0], Result[1], Result[2], Result[3], Result[4], Result[5], Result[6], Result[7], Result[8], Result[9], Result[10], Result[11], Result[12], Result[13], Result[14], Result[15], Result[16], Result[17], Result[18], Result[19], Result[20], Result[21], Result[22], Result[23], Result[24], Result[25], Result[26], Result[27]);
endmodule

module Control_Unit (
  input  [4:0] Opcode,
  output RegWRT,
  output RegDST,
  output AluSRC,
  output MemREAD,
  output MemWRT,
  output [1:0] MemToReg,
  output Branch,
  output BNE,
  output Jump,
  output SignZero,
  output [2:0] AluOP,
  output Binv
);

  wire decoder_1_out1, decoder_1_out2, decoder_1_out3, decoder_1_out4, decoder_1_out5, decoder_1_out7,
       decoder_1_out8, decoder_1_out9, decoder_1_out10, decoder_1_out13, decoder_1_out14, decoder_1_out16;

  extra extra_1 ();
  Decoder #(.select(5), .enable("false")) decoder_1 (
    .out0(MemREAD), .out1(decoder_1_out1), .out2(decoder_1_out2), .out3(decoder_1_out3),
    .out4(decoder_1_out4), .out5(decoder_1_out5), .out6(MemWRT), .out7(decoder_1_out7),
    .out8(decoder_1_out8), .out9(decoder_1_out9), .out10(decoder_1_out10), .out11(Branch), .out12(BNE),
    .out13(decoder_1_out13), .out14(decoder_1_out14), .out15(Jump), .out16(decoder_1_out16), .sel(Opcode));  // open: out17, out18, out19, out20, out21, out22, out23, out24, out25, out26, out27, out28, out29, out30, out31
  or or_1 (AluOP[0], decoder_1_out2, decoder_1_out4, decoder_1_out8, decoder_1_out9, Branch, BNE, decoder_1_out14);
  or or_2 (AluOP[1], MemREAD, decoder_1_out1, decoder_1_out2, decoder_1_out5, MemWRT, decoder_1_out9, Branch, BNE);
  or or_3 (AluOP[2], decoder_1_out7, decoder_1_out8);
  or or_4 (Binv, decoder_1_out2, decoder_1_out9, Branch, BNE);
  or or_5 (MemToReg[1], MemREAD, decoder_1_out10);
  or or_6 (RegWRT, MemREAD, decoder_1_out1, decoder_1_out2, decoder_1_out3, decoder_1_out4, decoder_1_out5, decoder_1_out7, decoder_1_out8, decoder_1_out9, decoder_1_out10, decoder_1_out13, decoder_1_out14, decoder_1_out16);
  or or_7 (RegDST, decoder_1_out1, decoder_1_out2, decoder_1_out3, decoder_1_out4, decoder_1_out7, decoder_1_out8, decoder_1_out10, decoder_1_out13);
  or or_8 (AluSRC, MemREAD, decoder_1_out5, MemWRT, decoder_1_out9, decoder_1_out14, decoder_1_out16);
  or or_9 (MemToReg[0], MemREAD, decoder_1_out3);
  or or_10 (SignZero, decoder_1_out16, decoder_1_out14);

  // Notes on the sheet:
  //   D7,D8
  //   D2,D9,D11,D12
  //   D2, D4, D8, D9, D11, D12, D14
  //   D0, D1, D2, D5, D6, D9, D11, D12
  //   D1, D2, D3, D4, D7, D8, D10, D13
  //   D0, D5, D6, D9, D14, D16
  //   D14,D16
  //   D0, D1, D2, D3, D4, D5, D7, D8, D9, D10, D13, D14, D16
endmodule

module Instruction_Memory (
  input  [6:0] Address,
  output [19:0] Instruction
);

  ROM #(.addrWidth(7), .dataWidth(20)) rom_1 (.addr(Address), .data(Instruction));  // open: sel
endmodule

module Data_Memory (
  input  [8:0] ADDRESS,
  input  [27:0] Write_Data,
  input  Clr,
  input  in_4,
  input  STR,
  input  Load,
  output [27:0] ReadData
);

  RAM #(.addrWidth(9), .dataWidth(28), .bus("separate")) ram_1 (
    .addr(ADDRESS), .din(Write_Data), .data(ReadData), .str(STR), .clk(in_4), .ld(Load), .clr(Clr));  // open: sel
endmodule

module Datapath (
  output [4:0] opcode_in_binary,
  output [27:0] Result,
  output out_3
);

  wire and_1_out, and_2_out, clock_1_out, control_unit_1_alusrc, control_unit_1_binv, control_unit_1_bne,
       control_unit_1_branch, control_unit_1_jump, control_unit_1_memread, control_unit_1_memwrt,
       control_unit_1_regdst, control_unit_1_regwrt, control_unit_1_signzero, n28_bit_alu_1_zero_flag,
       not_1_out, or_1_out;
  wire [1:0] control_unit_1_memtoreg;
  wire [2:0] control_unit_1_aluop;
  wire [4:0] multiplexer_1_out;
  wire [6:0] adder_1_out, adder_2_out, bit_extender_2_out, bit_extender_3_out, multiplexer_3_out,
       multiplexer_5_out, register_1_q;
  wire [19:5] rom_1_data;
  wire [27:0] bit_extender_1_out, multiplexer_2_out, n28_bit_alu_1_result, ram_1_data,
       register_file_1_read_data_1, register_file_1_read_data_2, shifter_1_out, shifter_2_out;

  Clock clock_1 (.out(clock_1_out));
  Register #(.width(7)) register_1 (.D(multiplexer_5_out), .Q(register_1_q), .clk(clock_1_out));  // open: en, clr
  Adder #(.width(7)) adder_1 (.a(register_1_q), .b(7'b0000001), .out(adder_1_out), .cin(1'b0));  // open: cout
  ROM #(.addrWidth(7), .dataWidth(20)) rom_1 (.addr(register_1_q), .data({rom_1_data, opcode_in_binary}));  // open: sel
  Control_Unit control_unit_1 (
    .Opcode(opcode_in_binary), .RegWRT(control_unit_1_regwrt), .RegDST(control_unit_1_regdst),
    .AluSRC(control_unit_1_alusrc), .MemREAD(control_unit_1_memread), .MemWRT(control_unit_1_memwrt),
    .MemToReg(control_unit_1_memtoreg), .Branch(control_unit_1_branch), .BNE(control_unit_1_bne),
    .Jump(control_unit_1_jump), .SignZero(control_unit_1_signzero), .AluOP(control_unit_1_aluop),
    .Binv(control_unit_1_binv));
  Multiplexer #(.width(5), .enable("false")) multiplexer_1 (
    .in0(rom_1_data[19:15]), .in1(rom_1_data[14:10]), .out(multiplexer_1_out), .sel(control_unit_1_regdst));
  Register_File register_file_1 (
    .Write_Reg_RD(multiplexer_1_out), .Write_Data(Result), .Read_Data_1(register_file_1_read_data_1),
    .Read_Reg_1_RS(rom_1_data[9:5]), .Read_Data_2(register_file_1_read_data_2),
    .Read_Reg_2_RT(rom_1_data[14:10]), .Write_Control(control_unit_1_regwrt), .CLK(clock_1_out));
  assign bit_extender_1_out = {{23{control_unit_1_signzero}}, rom_1_data[19:15]};  // Bit_Extender bit_extender_1
  Multiplexer #(.width(28), .enable("false")) multiplexer_2 (
    .in0(register_file_1_read_data_2), .in1(bit_extender_1_out), .out(multiplexer_2_out),
    .sel(control_unit_1_alusrc));
  assign bit_extender_2_out = {{2{1'b0}}, rom_1_data[19:15]};  // Bit_Extender bit_extender_2
  _28_bit_ALU u_28_bit_alu_1 (
    .Result(n28_bit_alu_1_result), .Zero_Flag(n28_bit_alu_1_zero_flag), .A(register_file_1_read_data_1),
    .B(multiplexer_2_out), .Select(control_unit_1_aluop), .Cin(control_unit_1_binv),
    .Binv(control_unit_1_binv), .Cout(out_3));  // open: Overflow
  Shifter #(.width(28)) shifter_1 (.in(register_file_1_read_data_1), .\dist (rom_1_data[19:15]), .out(shifter_1_out));
  Shifter #(.width(28), .shift("lr")) shifter_2 (
    .in(register_file_1_read_data_1), .\dist (rom_1_data[19:15]), .out(shifter_2_out));
  Adder #(.width(7)) adder_2 (.a(adder_1_out), .b(bit_extender_2_out), .out(adder_2_out));  // open: cin, cout
  not not_1 (not_1_out, n28_bit_alu_1_zero_flag);
  and and_1 (and_1_out, n28_bit_alu_1_zero_flag, control_unit_1_branch);
  and and_2 (and_2_out, not_1_out, control_unit_1_bne);
  assign bit_extender_3_out = {{2{1'b0}}, rom_1_data[19:15]};  // Bit_Extender bit_extender_3
  or or_1 (or_1_out, and_1_out, and_2_out);
  RAM #(.addrWidth(9), .dataWidth(28), .bus("separate")) ram_1 (
    .addr(n28_bit_alu_1_result[8:0]), .din(register_file_1_read_data_2), .data(ram_1_data),
    .str(control_unit_1_memwrt), .clk(clock_1_out), .ld(control_unit_1_memread));  // open: sel, clr
  Multiplexer #(.width(7), .enable("false")) multiplexer_3 (
    .in0(adder_1_out), .in1(adder_2_out), .out(multiplexer_3_out), .sel(or_1_out));
  Multiplexer #(.select(2), .width(28), .enable("false")) multiplexer_4 (
    .in0(n28_bit_alu_1_result), .in1(shifter_1_out), .in2(shifter_2_out), .in3(ram_1_data), .out(Result),
    .sel(control_unit_1_memtoreg));
  Multiplexer #(.width(7), .enable("false")) multiplexer_5 (
    .in0(multiplexer_3_out), .in1(bit_extender_3_out), .out(multiplexer_5_out), .sel(control_unit_1_jump));

  // Notes on the sheet:
  //   contents of rom_1 (hex, n*v repeats v):
  //   0 1 2 3 4 5 6 7 8 9 a b c d e f 10
  //   shift left
  //   shift right
  //   Alu Bits - 28
  //   ISA - 20
  //   Group 3
  //   Ins Mem Size- 128 - 2^7(7 bits)
  //   Data Memory - 384-2^9(9 bits)
endmodule
